// Logisim project microOrgaSmallwithStack.circ as structural Verilog: 7 circuits, main circuit microOrgaSmall
module microOrgaSmall (
  input  reset,
  input  mem_clear
);

  wire ALU_enA, ALU_enB, ALU_enOut, ALU_opW, button_1_out, button_2_out, button_3_out, clk, clock_1_out, clr,
       DE_enOutImm, DE_load_7_0, DE_load_15_8, MM_enAddr, MM_enOut, MM_load, PC_enOut, PC_inc, PC_load,
       RB_enIn, RB_enOut, RB_selectIndexIn, RB_selectIndexOut, rst;
  wire [2:0] multiplexer_1_out, multiplexer_2_out, X, Y;
  wire [3:0] ALU_OP, flags, PC_outvalue, PC_outvalue_2;
  wire [4:0] OP;
  wire [7:0] A, B, M, O, PC;
  wire [8:0] M_PC;
  wire [15:0] INST;
  wire [31:0] R0_3, R4_7;

  PC u_PC (
    .load(PC_load), .inc(PC_inc), .outValue({PC_outvalue_2, PC_outvalue}), .enOut(PC_enOut), .VIEW_value(PC),
    .clk(clk), .rst(rst), .inValue({PC_outvalue_2, PC_outvalue}));
  Registers Registers (
    .clk(clk), .rst(rst), .inData({PC_outvalue_2, PC_outvalue}), .outData({PC_outvalue_2, PC_outvalue}),
    .enIn(RB_enIn), .enOut(RB_enOut), .inSelect(multiplexer_1_out), .outSelect(multiplexer_2_out),
    .VIEW_R4_R7(R4_7), .VIEW_R0_R3(R0_3));
  Memory Memory (
    .addr({PC_outvalue_2, PC_outvalue}), .load(MM_load), .outData({PC_outvalue_2, PC_outvalue}),
    .enOut(MM_enOut), .clk(clk), .rst(rst), .inData({PC_outvalue_2, PC_outvalue}), .enAddr(MM_enAddr),
    .clr(clr));  // open: outAddr
  assign {PC_outvalue_2, PC_outvalue} = DE_enOutImm ? M : 8'bz;  // Controlled_Buffer controlled_buffer_1
  Decode Decode (
    .indexX(X), .indexY(Y), .valueM(M), .opcode(OP), .clk(clk), .rst(rst),
    .halfInst({PC_outvalue_2, PC_outvalue}), .loadH(DE_load_15_8), .loadL(DE_load_7_0), .VIEW_Inst(INST));
  Hex_Digit_Display hex_digit_display_1 (.value(PC_outvalue_2));  // open: dp
  Multiplexer #(.width(3), .enable("false")) multiplexer_1 (
    .in0(X), .in1(Y), .out(multiplexer_1_out), .sel(RB_selectIndexIn));
  Multiplexer #(.width(3), .enable("false")) multiplexer_2 (
    .in0(X), .in1(Y), .out(multiplexer_2_out), .sel(RB_selectIndexOut));
  Hex_Digit_Display hex_digit_display_2 (.value(PC_outvalue));  // open: dp
  ALU alu_1 (
    .A({PC_outvalue_2, PC_outvalue}), .enA(ALU_enA), .B({PC_outvalue_2, PC_outvalue}), .enB(ALU_enB),
    .OP(ALU_OP), .out({PC_outvalue_2, PC_outvalue}), .enOut(ALU_enOut), .VIEW_out(O), .VIEW_A(A), .VIEW_B(B),
    .clk(clk), .rst(rst), .shift(Y), .flagsOut(flags), .write_op(ALU_opW));
  ControlUnit ControlUnit (
    .RB_enIn(RB_enIn), .RB_enOut(RB_enOut), .RB_selectIndexIn(RB_selectIndexIn),
    .RB_selectIndexOut(RB_selectIndexOut), .MM_enOut(MM_enOut), .MM_load(MM_load), .MM_enAddr(MM_enAddr),
    .ALU_enA(ALU_enA), .ALU_enB(ALU_enB), .ALU_enOut(ALU_enOut), .ALU_OP(ALU_OP), .ALU_opW(ALU_opW),
    .PC_load(PC_load), .PC_inc(PC_inc), .PC_enOut(PC_enOut), .DE_loadH(DE_load_15_8), .inOpcode(OP),
    .DE_enOutImm(DE_enOutImm), .VIEW_microOpAddr(M_PC), .clk(clk), .rst(rst), .flags(flags),
    .DE_loadL(DE_load_7_0));
  LED Z (.in(flags[1]));
  LED u_O (.in(flags[3]));
  LED N (.in(flags[2]));
  Hex_Digit_Display hex_digit_display_3 (.value(INST[15:12]));  // open: dp
  Hex_Digit_Display hex_digit_display_4 (.value(M[7:4]));  // open: dp
  LED C (.in(flags[0]));
  Hex_Digit_Display hex_digit_display_5 (.value(R0_3[3:0]));  // open: dp
  Hex_Digit_Display hex_digit_display_6 (.value(R0_3[7:4]));  // open: dp
  Hex_Digit_Display hex_digit_display_7 (.value(R0_3[15:12]));  // open: dp
  Hex_Digit_Display hex_digit_display_8 (.value(R0_3[11:8]));  // open: dp
  Hex_Digit_Display hex_digit_display_9 (.value(R0_3[23:20]));  // open: dp
  Hex_Digit_Display hex_digit_display_10 (.value(R0_3[19:16]));  // open: dp
  Hex_Digit_Display hex_digit_display_11 (.value(R0_3[27:24]));  // open: dp
  Hex_Digit_Display hex_digit_display_12 (.value(R0_3[31:28]));  // open: dp
  Hex_Digit_Display hex_digit_display_13 (.value(INST[11:8]));  // open: dp
  Hex_Digit_Display hex_digit_display_14 (.value(INST[7:4]));  // open: dp
  Hex_Digit_Display hex_digit_display_15 (.value(M[3:0]));  // open: dp
  Button button_1 (.out(button_1_out));
  Clock clock_1 (.out(clock_1_out));
  Hex_Digit_Display hex_digit_display_16 (.value(INST[3:0]));  // open: dp
  Hex_Digit_Display hex_digit_display_17 (.value({1'b0, X}));  // open: dp
  Button button_2 (.out(button_2_out));
  or or_1 (clk, button_1_out, clock_1_out);
  Hex_Digit_Display hex_digit_display_18 (.value(R4_7[7:4]));  // open: dp
  Hex_Digit_Display hex_digit_display_19 (.value(R4_7[3:0]));  // open: dp
  Hex_Digit_Display hex_digit_display_20 (.value(R4_7[15:12]));  // open: dp
  Hex_Digit_Display hex_digit_display_21 (.value(R4_7[11:8]));  // open: dp
  Hex_Digit_Display hex_digit_display_22 (.value(R4_7[19:16]));  // open: dp
  Hex_Digit_Display hex_digit_display_23 (.value(R4_7[23:20]));  // open: dp
  Hex_Digit_Display hex_digit_display_24 (.value(R4_7[27:24]));  // open: dp
  Hex_Digit_Display hex_digit_display_25 (.value(R4_7[31:28]));  // open: dp
  Hex_Digit_Display hex_digit_display_26 (.value({3'b000, M_PC[8]}));  // open: dp
  Hex_Digit_Display hex_digit_display_27 (.value({1'b0, Y}));  // open: dp
  or or_2 (rst, button_2_out, reset);
  Hex_Digit_Display hex_digit_display_28 (.value(M_PC[3:0]));  // open: dp
  Hex_Digit_Display hex_digit_display_29 (.value(M_PC[7:4]));  // open: dp
  Hex_Digit_Display hex_digit_display_30 (.value({3'b000, OP[4]}));  // open: dp
  Button button_3 (.out(button_3_out));
  or or_3 (clr, button_3_out, mem_clear);
  Hex_Digit_Display hex_digit_display_31 (.value(PC[7:4]));  // open: dp
  Hex_Digit_Display hex_digit_display_32 (.value(PC[3:0]));  // open: dp
  Hex_Digit_Display hex_digit_display_33 (.value(A[7:4]));  // open: dp
  Hex_Digit_Display hex_digit_display_34 (.value(A[3:0]));  // open: dp
  Hex_Digit_Display hex_digit_display_35 (.value(B[7:4]));  // open: dp
  Hex_Digit_Display hex_digit_display_36 (.value(B[3:0]));  // open: dp
  Hex_Digit_Display hex_digit_display_37 (.value(O[7:4]));  // open: dp
  Hex_Digit_Display hex_digit_display_38 (.value(O[3:0]));  // open: dp
  Hex_Digit_Display hex_digit_display_39 (.value(OP[3:0]));  // open: dp

  // Notes on the sheet:
  //   BUS
  //   Instruction
  //   value M
  //   R0
  //   R1
  //   R2
  //   R3
  //   index X
  //   index Y
  //   R4
  //   R5
  //   R6
  //   R7
  //   microPC
  //   PC
  //   Opcode
  //   A
  //   B
  //   OUT
endmodule

module Registers (
  input  clk,
  input  rst,
  input  [7:0] inData,
  input  enOut,
  input  enIn,
  input  [2:0] outSelect,
  input  [2:0] inSelect,
  output [31:0] VIEW_R0_R3,
  output [31:0] VIEW_R4_R7,
  output [7:0] outData
);

  wire decoder_1_out0, decoder_1_out1, decoder_1_out2, decoder_1_out3, decoder_1_out4, decoder_1_out5,
       decoder_1_out6, decoder_1_out7;
  wire [7:0] multiplexer_1_out;

  Decoder #(.select(3), .disabled(0)) decoder_1 (
    .out0(decoder_1_out0), .out1(decoder_1_out1), .out2(decoder_1_out2), .out3(decoder_1_out3),
    .out4(decoder_1_out4), .out5(decoder_1_out5), .out6(decoder_1_out6), .out7(decoder_1_out7),
    .sel(inSelect), .en(enIn));
  Register R0 (.D(inData), .en(decoder_1_out0), .Q(VIEW_R0_R3[7:0]), .clk(clk), .clr(rst));
  Register R1 (.D(inData), .en(decoder_1_out1), .Q(VIEW_R0_R3[15:8]), .clk(clk), .clr(rst));
  Register R2 (.D(inData), .en(decoder_1_out2), .Q(VIEW_R0_R3[23:16]), .clk(clk), .clr(rst));
  Register R3 (.D(inData), .en(decoder_1_out3), .Q(VIEW_R0_R3[31:24]), .clk(clk), .clr(rst));
  Register R4 (.D(inData), .en(decoder_1_out4), .Q(VIEW_R4_R7[7:0]), .clk(clk), .clr(rst));
  Register R5 (.D(inData), .en(decoder_1_out5), .Q(VIEW_R4_R7[15:8]), .clk(clk), .clr(rst));
  Register R6 (.D(inData), .en(decoder_1_out6), .Q(VIEW_R4_R7[23:16]), .clk(clk), .clr(rst));
  Register R7 (.D(inData), .en(decoder_1_out7), .Q(VIEW_R4_R7[31:24]), .clk(clk), .clr(rst));
  Multiplexer #(.select(3), .width(8), .enable("false")) multiplexer_1 (
    .in0(VIEW_R0_R3[7:0]), .in1(VIEW_R0_R3[15:8]), .in2(VIEW_R0_R3[23:16]), .in3(VIEW_R0_R3[31:24]),
    .in4(VIEW_R4_R7[7:0]), .in5(VIEW_R4_R7[15:8]), .in6(VIEW_R4_R7[23:16]), .in7(VIEW_R4_R7[31:24]),
    .out(multiplexer_1_out), .sel(outSelect));
  assign outData = enOut ? multiplexer_1_out : 8'bz;  // Controlled_Buffer controlled_buffer_1
endmodule

module PC (
  input  clk,
  input  rst,
  input  load,
  input  [7:0] inValue,
  input  inc,
  input  enOut,
  output [7:0] VIEW_value,
  output [7:0] outValue
);

  assign outValue = enOut ? VIEW_value : 8'bz;  // Controlled_Buffer controlled_buffer_1
  Counter counter_1 (.load(load), .D(inValue), .count(inc), .Q(VIEW_value), .clk(clk), .clr(rst));  // open: carry
endmodule

module ALU (
  input  clk,
  input  rst,
  input  [7:0] A,
  input  enA,
  input  [7:0] B,
  input  write_op,
  input  enB,
  input  enOut,
  input  [2:0] shift,
  input  [3:0] OP,
  output [3:0] flagsOut,
  output [7:0] out,
  output [7:0] VIEW_out,
  output [7:0] VIEW_A,
  output [7:0] VIEW_B
);

  wire and_2_out, and_4_out, and_5_out, and_6_out, C, multiplexer_4_out, N, not_1_out, not_2_out, not_3_out,
       not_4_out, not_5_out, not_6_out, O, O_E10, or_1_out, or_3_out, or_5_out, or_6_out, subtractor_1_bout,
       subtractor_2_bout, xor_2_out, Z;
  wire [1:1] and_3_out;
  wire [3:0] multiplexer_1_out;
  wire [7:0] adder_2_out, and_1_out, multiplexer_5_out, multiplexer_6_out, or_2_out, shifter_1_out,
       shifter_2_out, shifter_3_out, xor_1_out;
  wire [8:0] adder_1_out, adder_3_out, adder_4_out, multiplexer_2_out, subtractor_1_out, subtractor_2_out,
       subtractor_3_out;

  Register ALU_IN_A (.D(A), .en(enA), .Q(VIEW_A), .clk(clk), .clr(rst));
  Register ALU_IN_B (.D(B), .en(enB), .Q(VIEW_B), .clk(clk), .clr(rst));
  Subtractor #(.width(9)) subtractor_1 (
    .a({1'b0, VIEW_A}), .b(9'ha), .out(subtractor_1_out), .bout(subtractor_1_bout));  // open: bin
  Subtractor #(.width(9)) subtractor_2 (
    .a({1'b0, VIEW_B}), .b(9'ha), .out(subtractor_2_out), .bout(subtractor_2_bout));  // open: bin
  Adder #(.width(9)) adder_1 (.a(subtractor_1_out), .b(subtractor_2_out), .out(adder_1_out), .cin(1'b0));  // open: cout
  or or_1 (or_1_out, subtractor_1_bout, subtractor_2_bout);
  assign and_1_out = VIEW_A & VIEW_B;  // AND_Gate and_1, 8 bits wide
  assign or_2_out = VIEW_A | VIEW_B;  // OR_Gate or_2, 8 bits wide
  assign xor_1_out = VIEW_A ^ VIEW_B;  // XOR_Gate xor_1, 8 bits wide
  Shifter #(.shift("ar")) shifter_1 (.in(VIEW_A), .\dist (shift), .out(shifter_1_out));
  Shifter #(.shift("lr")) shifter_2 (.in(VIEW_A), .\dist (shift), .out(shifter_2_out));
  Shifter shifter_3 (.in(VIEW_A), .\dist (shift), .out(shifter_3_out));
  Adder #(.width(9)) adder_2 (.a(adder_1_out), .b(9'ha), .out({O_E10, adder_2_out}));  // open: cin, cout
  and and_2 (and_2_out, OP[3], ~OP[2], OP[1], OP[0]);  // AND_Gate
  Adder #(.width(9)) adder_3 (.a({1'b0, VIEW_A}), .b({1'b0, VIEW_B}), .out(adder_3_out), .cin(1'b0));  // open: cout
  Adder #(.width(9)) adder_4 (
    .a({1'b0, VIEW_A}), .b({1'b0, VIEW_B}), .out(adder_4_out), .cin(flagsOut[0]));  // open: cout
  Subtractor #(.width(9)) subtractor_3 (
    .a({1'b0, VIEW_A}), .b({1'b0, VIEW_B}), .out(subtractor_3_out), .bin(1'b0));  // open: bout
  Multiplexer #(.width(4), .enable("false")) multiplexer_1 (
    .in0({O, N, Z, C}), .in1(VIEW_A[3:0]), .out(multiplexer_1_out), .sel(and_2_out));
  and and_3 (and_3_out[1], O_E10, or_1_out);
  Register #(.width(1)) u_C (.D(multiplexer_1_out[0]), .en(or_3_out), .Q(flagsOut[0]), .clk(not_1_out), .clr(rst));
  or or_3 (or_3_out, and_2_out, write_op);
  not not_1 (not_1_out, clk);
  or or_4 (O, and_5_out, and_4_out);
  or or_5 (or_5_out, OP[2], OP[3]);
  Multiplexer #(.select(2), .width(9), .enable("false")) multiplexer_2 (
    .in0({9{1'b0}}), .in1(adder_3_out), .in2(adder_4_out), .in3(subtractor_3_out), .out(multiplexer_2_out),
    .sel(OP[1:0]));
  Register #(.width(1)) u_Z (.D(multiplexer_1_out[1]), .en(or_3_out), .Q(flagsOut[1]), .clk(not_2_out), .clr(rst));
  not not_2 (not_2_out, clk);
  and and_4 (and_4_out, multiplexer_4_out, not_3_out);
  not not_3 (not_3_out, or_5_out);
  Multiplexer #(.enable("false")) multiplexer_3 (.in0(multiplexer_2_out[8]), .in1(1'b0), .out(C), .sel(or_5_out));
  Register #(.width(1)) u_N (.D(multiplexer_1_out[2]), .en(or_3_out), .Q(flagsOut[2]), .clk(not_4_out), .clr(rst));
  not not_4 (not_4_out, clk);
  Multiplexer #(.enable("false")) multiplexer_4 (.in0(xor_2_out), .in1(1'b0), .out(multiplexer_4_out), .sel(or_5_out));
  xor xor_2 (xor_2_out, multiplexer_2_out[8], multiplexer_2_out[7]);
  Multiplexer #(.select(2), .width(8), .enable("false")) multiplexer_5 (
    .in0(adder_2_out), .in2({8{1'b1}}), .in3({8{1'b0}}), .out(multiplexer_5_out), .sel({and_3_out[1], O_E10}));  // open: in1
  Register #(.width(1)) u_O (.D(multiplexer_1_out[3]), .en(or_3_out), .Q(flagsOut[3]), .clk(not_5_out), .clr(rst));
  not not_5 (not_5_out, clk);
  and and_5 (and_5_out, O_E10, ~OP[0], OP[1], OP[2], OP[3]);  // AND_Gate
  Multiplexer #(.select(4), .width(8), .enable("false")) multiplexer_6 (
    .in0({8{1'b0}}), .in1(multiplexer_2_out[7:0]), .in2(multiplexer_2_out[7:0]),
    .in3(multiplexer_2_out[7:0]), .in4(and_1_out), .in5(or_2_out), .in6(xor_1_out), .in7(shifter_1_out),
    .in8(shifter_2_out), .in9(shifter_3_out), .in10({4'b0000, flagsOut}), .in12({8{1'b0}}), .in13(8'h1),
    .in14(multiplexer_5_out), .in15({8{1'b1}}), .out(multiplexer_6_out), .sel(OP));  // open: in11
  or or_6 (or_6_out, OP[3], OP[2], OP[1], OP[0]);
  and and_6 (and_6_out, ~OP[0], OP[1], OP[2], OP[3]);  // AND_Gate
  nor nor_1 (Z, multiplexer_6_out[7], multiplexer_6_out[6], multiplexer_6_out[5], multiplexer_6_out[4], multiplexer_6_out[3], multiplexer_6_out[2], multiplexer_6_out[1], multiplexer_6_out[0]);
  Register ALU_OUT (.D(multiplexer_6_out), .en(or_6_out), .Q(VIEW_out), .clk(not_6_out), .clr(rst));
  not not_6 (not_6_out, clk);
  Multiplexer #(.enable("false")) multiplexer_7 (.in0(multiplexer_6_out[7]), .out(N), .sel(and_6_out));  // open: in1
  assign out = enOut ? VIEW_out : 8'bz;  // Controlled_Buffer controlled_buffer_1

  // Other names for the same wires on the sheet: A_t[7:0] = VIEW_A; B_t[7:0] = VIEW_B; carry_flag = flagsOut[0];
  //   flags[3:0] = flagsOut

  // Notes on the sheet:
  //   ADDE10S
  //   LOAD_FLAGS = 1011
  //   ADD = 0001
  //   ADC = 0010
  //   SUB = 0011
  //   cte 0x00 = 1100
  //   cte 0x01 = 1101
  //   cte 0xFF = 1111
  //   CONSTANTES
  //   AND = 0100
  //   OR = 0101
  //   XOR =0110
  //    SHRA = 0111
  //   SHR = 1000
  //   SHL = 1001
  //   READ_FLAGS = 1011
endmodule

module Memory (
  input  clk,
  input  rst,
  input  clr,
  input  [7:0] addr,
  input  enAddr,
  input  [7:0] inData,
  input  enOut,
  input  load,
  output [7:0] outAddr,
  output [7:0] outData
);

  wire [7:0] ram_1_data;

  Register u_addr (.D(addr), .en(enAddr), .Q(outAddr), .clk(clk), .clr(rst));
  RAM #(.bus("separate")) ram_1 (
    .addr(outAddr), .din(inData), .data(ram_1_data), .str(load), .clk(clk), .clr(clr));  // open: sel, ld
  assign outData = enOut ? ram_1_data : 8'bz;  // Controlled_Buffer controlled_buffer_1
endmodule

module Decode (
  input  clk,
  input  rst,
  input  [7:0] halfInst,
  input  loadL,
  input  loadH,
  output [4:0] opcode,
  output [2:0] indexX,
  output [2:0] indexY,
  output [7:0] valueM,
  output [15:0] VIEW_Inst
);

  Register IR_7_0 (.D(halfInst), .en(loadL), .Q(VIEW_Inst[7:0]), .clk(clk), .clr(rst));
  Register IR_15_8 (.D(halfInst), .en(loadH), .Q(VIEW_Inst[15:8]), .clk(clk), .clr(rst));
  Register #(.width(5)) u_opcode (.D(VIEW_Inst[15:11]), .en(1'b1), .Q(opcode), .clk(clk), .clr(rst));
  Register #(.width(3)) index_X (.D(VIEW_Inst[10:8]), .en(1'b1), .Q(indexX), .clk(clk), .clr(rst));
  Register #(.width(3)) index_Y (.D(VIEW_Inst[7:5]), .en(1'b1), .Q(indexY), .clk(clk), .clr(rst));
  Register Mem_Or_Imm (.D(VIEW_Inst[7:0]), .en(1'b1), .Q(valueM), .clk(clk), .clr(rst));
endmodule

module ControlUnit (
  input  clk,
  input  rst,
  input  [3:0] flags,
  input  [4:0] inOpcode,
  output RB_enIn,
  output RB_enOut,
  output RB_selectIndexIn,
  output RB_selectIndexOut,
  output MM_enOut,
  output MM_load,
  output MM_enAddr,
  output ALU_enA,
  output ALU_enB,
  output ALU_enOut,
  output ALU_opW,
  output [3:0] ALU_OP,
  output PC_load,
  output PC_inc,
  output PC_enOut,
  output DE_enOutImm,
  output DE_loadL,
  output DE_loadH,
  output [8:0] VIEW_microOpAddr
);

  wire and_1_out, and_2_out, and_3_out, and_4_out, jc_microOp, jn_microOp, jo_microOp, jz_microOp,
       load_microOp, not_1_out, or_1_out, or_2_out, or_3_out, reset_microOp;
  wire [8:0] adder_1_out, adder_2_out, multiplexer_1_out, multiplexer_2_out;
  wire [29:4] rom_1_data;

  Counter #(.width(9), .max('h1ff)) microPC (
    .load(load_microOp), .D(multiplexer_2_out), .count(not_1_out), .Q(VIEW_microOpAddr), .clk(clk),
    .clr(or_1_out));  // open: carry
  not not_1 (not_1_out, load_microOp);
  or or_1 (or_1_out, reset_microOp, rst);
  and and_1 (and_1_out, flags[2], jn_microOp);
  and and_2 (and_2_out, flags[3], jo_microOp);
  Adder #(.width(9)) adder_1 (.a(VIEW_microOpAddr), .b(9'h1), .out(adder_1_out), .cin(1'b0));  // open: cout
  Adder #(.width(9)) adder_2 (.a(VIEW_microOpAddr), .b(9'h2), .out(adder_2_out), .cin(1'b0));  // open: cout
  and and_3 (and_3_out, flags[0], jc_microOp);
  and and_4 (and_4_out, flags[1], jz_microOp);
  or or_2 (or_2_out, and_2_out, and_1_out, and_4_out, and_3_out);
  Multiplexer #(.width(9), .enable("false")) multiplexer_1 (
    .in0(adder_1_out), .in1(adder_2_out), .out(multiplexer_1_out), .sel(or_2_out));
  or or_3 (or_3_out, jo_microOp, jn_microOp, jz_microOp, jc_microOp);
  Multiplexer #(.width(9), .enable("false")) multiplexer_2 (
    .in0({inOpcode, 4'b0000}), .in1(multiplexer_1_out), .out(multiplexer_2_out), .sel(or_3_out));
  ROM #(.addrWidth(9), .dataWidth(32)) rom_1 (
    .addr(VIEW_microOpAddr),
    .data({reset_microOp, load_microOp, rom_1_data[29:27], DE_loadH, DE_loadL, DE_enOutImm, rom_1_data[23], PC_enOut, PC_inc, PC_load, jo_microOp, jn_microOp, jz_microOp, jc_microOp, ALU_OP, ALU_opW, ALU_enOut, ALU_enB, ALU_enA, MM_enAddr, MM_load, MM_enOut, rom_1_data[4], RB_selectIndexOut, RB_selectIndexIn, RB_enOut, RB_enIn}));  // open: sel

  // Notes on the sheet:
  //   contents of rom_1 (hex, n*v repeats v):
  //   400080 4200020 400080 2200020 40000000 80000000 10*0 102 20a 1800 401 80000000 11*0 102 20a 2800 401
  //   80000000 11*0 102 20a 3800 401 80000000 11*0 102 20a 4800 401 80000000 11*0 102 20a 5800 401
  //   80000000 11*0 102 20a 6800 401 80000000 11*0 102 20a 3800 80000000 12*0 b 80000000 14*0 82 4a 102
  //   d600 3401 80000000 10*0 102 d600 1401 82 25 80000000 10*0 82 400040 102 d600 3401 10000a 80000000
  //   9*0 82 400040 102 d600 3401 1100000 80000000 9*0 102 d600 1401 82 100020 80000000 10*0 102 d600 1480
  //   220 82 120 1800 440 80000000 7*0 102 20a e800 401 80000000 11*0 1000080 42 80000000 13*0 1000080 21
  //   80000000 13*0 82 4a 80000000 13*0 8a 21 80000000 13*0 1100000 80000000 14*0 40010000 80000000
  //   1100000 80000000 12*0 40020000 80000000 1100000 80000000 12*0 40040000 80000000 1100000 80000000
  //   12*0 40080000 80000000 1100000 80000000 12*0 102 7c01 80000000 13*0 102 8c01 80000000 13*0 102 9c01
  //   80000000 13*0 a000 401 80000000 13*0 102 b000 80000000 13*0 1000001 80000000 14*0 80000000
endmodule
